# Fritzing sketch diagram (saved by Fritzing 0.9.2b)
breadboards: 1

parts:
  Pro_Micro1 = SparkFun Pro Micro
  S1 = Pushbutton [package="[SMD]"]  # not connected
  S2 = Pushbutton [package="[SMD]"]  # not connected
  S3 = Pushbutton [package="[SMD]"]  # not connected
  S4 = Pushbutton [package="[SMD]"]  # not connected
  LED1 = LED - 3mm [color="White (6500K)" package="3 mm [THT]"]
  LED2 = LED - 3mm [color="Green (555nm)" package="3 mm [THT]"]
  LED3 = LED - 3mm [color="Yellow (585nm)" package="3 mm [THT]"]
  LED4 = LED - 3mm [color="Red (633nm)" package="3 mm [THT]"]
  R1 = Resistor [tolerance=±5% resistance=1k package="0603 [SMD]"]
  R2 = Resistor [tolerance=±5% resistance=1k package="0603 [SMD]"]
  R3 = Resistor [tolerance=±5% resistance=1k package="0603 [SMD]"]
  R4 = Resistor [tolerance=±5% resistance=1k package="0603 [SMD]"]
  IC1 = IC, DIP package, 8 pins [chip_label=Huskylens]

nets:
  N1: Pro_Micro1.2, IC1.pin8
  N2: Pro_Micro1.3, Pro_Micro1.4, IC1.pin7
  N3: Pro_Micro1.14, LED4.anode
  N4: Pro_Micro1.15, LED3.anode
  N5: Pro_Micro1.A2, LED2.anode
  N6: Pro_Micro1.A3, LED1.anode
  N7: LED1.cathode, R4.Pin_1
  N8: LED2.cathode, R3.Pin_1
  N9: LED3.cathode, R2.Pin_1
  N10: LED4.cathode, R1.Pin_1
  N11: R1.Pin_0, R2.Pin_0, R4.Pin_0, IC1.pin6

custom parts:
  SparkFun Pro Micro: The Pro Micro is similar to the Pro Mini except with an ATmega32U4 on board. The USB transceiver inside the 32U4 allows us to add USB connectivity on-board and do away with bulky external USB interface. Based on: https://github.com/unorthodox-engineers/unorthodox-arduino/blob/master/Unorthodox/fritzing/parts/Pro%20Micro.fzpz
